# Fritzing sketch connections (saved by Fritzing 0.9.5d)
breadboards: 1

parts:
  DHT11_1 = DHT11 module
  U1 = NodeMCU V3.0

nets:
  VCC: DHT11_1.VCC, U1.3V3
  GND: DHT11_1.GND, U1.GND
  N1: DHT11_1.DATA, U1.D2

notes:
  We used nodemcu in place for ses dev board. In the ses dev board you will have to connect to pin 15

custom parts:
  DHT11 module: DHT11 black pcb module
  NodeMCU V3.0: ESP8266 based NodeMCU
